// Logisim project experiment.circ as structural Verilog: 10 circuits, main circuit 主电路 / main
module \主电路___main  (
);

  wire buzzer_1_p2, K0_out, K1_out, K2_out, K3_out, \减分按钮___SUB_SCORE_out , \加分按钮___ADD_SCORE_out ,
       \定时开始按钮___TIMER_START_out , \定时模块_p5 , \定时模块_p9 , \总复位按钮___RESET_out ,
       \抢答判别模块_responder_latch_1_enable , \抢答判别模块_responder_latch_1_lock , \抢答判别模块_responder_latch_1_q0 ,
       \抢答判别模块_responder_latch_1_q1 , \抢答判别模块_responder_latch_1_q2 , \抢答判别模块_responder_latch_1_q3 ,
       \抢答开始按钮___QUIZ_START_out , \抢答指示灯和声音模块_led0 , \抢答指示灯和声音模块_led1 , \抢答指示灯和声音模块_led2 , \抢答指示灯和声音模块_led3 ,
       \抢答指示灯和声音模块_ready_led , \秒脉冲时钟___SEC_CLK_out , \蜂鸣时钟___BEEP_CLK_out , \闪烁时钟___FLASH_CLK_out ;
  wire [1:0] \小组选择___TEAM_SEL_p1 , \小组选择___TEAM_SEL_p3 ;
  wire [3:0] \定时模块_p6 , \定时模块_p7 , \总记分模块_score_board_1__1h , \总记分模块_score_board_1__1o ,
       \总记分模块_score_board_1__1t , \总记分模块_score_board_1__2h , \总记分模块_score_board_1__2o ,
       \总记分模块_score_board_1__2t , \总记分模块_score_board_1__3h , \总记分模块_score_board_1__3o ,
       \总记分模块_score_board_1__3t , \总记分模块_score_board_1__4h , \总记分模块_score_board_1__4o ,
       \总记分模块_score_board_1__4t ;

  Hex_Digit_Display hex_digit_display_1 (.value(\总记分模块_score_board_1__1t ));  // open: dp
  Hex_Digit_Display hex_digit_display_2 (.value(\总记分模块_score_board_1__1h ));  // open: dp
  Hex_Digit_Display hex_digit_display_3 (.value(\总记分模块_score_board_1__3t ));  // open: dp
  Hex_Digit_Display hex_digit_display_4 (.value(\总记分模块_score_board_1__3h ));  // open: dp
  Hex_Digit_Display hex_digit_display_5 (.value(\总记分模块_score_board_1__1o ));  // open: dp
  Hex_Digit_Display hex_digit_display_6 (.value(\总记分模块_score_board_1__3o ));  // open: dp
  Hex_Digit_Display hex_digit_display_7 (.value(\总记分模块_score_board_1__2t ));  // open: dp
  Hex_Digit_Display hex_digit_display_8 (.value(\总记分模块_score_board_1__2h ));  // open: dp
  Hex_Digit_Display hex_digit_display_9 (.value(\总记分模块_score_board_1__4h ));  // open: dp
  Hex_Digit_Display hex_digit_display_10 (.value(\总记分模块_score_board_1__4t ));  // open: dp
  Hex_Digit_Display hex_digit_display_11 (.value(\总记分模块_score_board_1__2o ));  // open: dp
  Hex_Digit_Display hex_digit_display_12 (.value(\总记分模块_score_board_1__4o ));  // open: dp
  LED led_1 (.in(\抢答指示灯和声音模块_led0 ));
  LED led_2 (.in(\抢答指示灯和声音模块_led1 ));
  LED led_3 (.in(\抢答指示灯和声音模块_led2 ));
  LED led_4 (.in(\抢答指示灯和声音模块_led3 ));
  // Buzzer buzzer_1: pin names not known; wires that end beside it: {12{1'b1}}, buzzer_1_p2, {7{1'b1}}
  LED \u_抢答等待闪烁灯  (.in(\抢答指示灯和声音模块_ready_led ));
  Button \u_抢答开始按钮___QUIZ_START  (.out(\抢答开始按钮___QUIZ_START_out ));
  Button \u_定时开始按钮___TIMER_START  (.out(\定时开始按钮___TIMER_START_out ));
  Button \u_总复位按钮___RESET  (.out(\总复位按钮___RESET_out ));
  Button K0 (.out(K0_out));
  Button K1 (.out(K1_out));
  Button K2 (.out(K2_out));
  Button K3 (.out(K3_out));
  Button \u_加分按钮___ADD_SCORE  (.out(\加分按钮___ADD_SCORE_out ));
  Button \u_减分按钮___SUB_SCORE  (.out(\减分按钮___SUB_SCORE_out ));
  // DipSwitch #(.NSwitches(2)) 定时时间选择___TIME_SEL: pin names not known; wires that end beside it: \小组选择___TEAM_SEL_p1 [1]
  // DipSwitch #(.NSwitches(2)) 小组选择___TEAM_SEL: pin names not known; wires that end beside it: \小组选择___TEAM_SEL_p1 [0], \小组选择___TEAM_SEL_p3 [1], \小组选择___TEAM_SEL_p3 [0]
  Clock #(.highDuration(8), .lowDuration(8)) \u_秒脉冲时钟___SEC_CLK  (.out(\秒脉冲时钟___SEC_CLK_out ));
  Clock \u_闪烁时钟___FLASH_CLK  (.out(\闪烁时钟___FLASH_CLK_out ));
  Clock #(.highDuration(8), .lowDuration(8)) \u_蜂鸣时钟___BEEP_CLK  (.out(\蜂鸣时钟___BEEP_CLK_out ));
  \抢答指示灯和声音模块___Responder_Indicator  \u_抢答指示灯和声音模块  (
    .LOCK(\抢答判别模块_responder_latch_1_lock ), .FLASH_CLK(\闪烁时钟___FLASH_CLK_out ),
    .BEEP_CLK(\蜂鸣时钟___BEEP_CLK_out ), .Q0(\抢答判别模块_responder_latch_1_q0 ), .Q1(\抢答判别模块_responder_latch_1_q1 ),
    .Q2(\抢答判别模块_responder_latch_1_q2 ), .Q3(\抢答判别模块_responder_latch_1_q3 ),
    .ENABLE(\抢答判别模块_responder_latch_1_enable ), .LED0(\抢答指示灯和声音模块_led0 ), .LED1(\抢答指示灯和声音模块_led1 ),
    .LED2(\抢答指示灯和声音模块_led2 ), .LED3(\抢答指示灯和声音模块_led3 ), .READY_LED(\抢答指示灯和声音模块_ready_led ),
    .BUZZER(buzzer_1_p2));
  // 定时模块___Timer 定时模块: pin names not known; wires that end beside it: \蜂鸣时钟___BEEP_CLK_out , \小组选择___TEAM_SEL_p1 , \定时开始按钮___TIMER_START_out , \总复位按钮___RESET_out , \定时模块_p5 , \定时模块_p6 , \定时模块_p7 , \秒脉冲时钟___SEC_CLK_out , \定时模块_p9 
  \抢答判别模块___Responder_Latch  \u_抢答判别模块_responder_latch_1  (
    .START(\抢答开始按钮___QUIZ_START_out ), .RESET(\总复位按钮___RESET_out ), .K0(K0_out),
    .Q0(\抢答判别模块_responder_latch_1_q0 ), .K1(K1_out), .Q1(\抢答判别模块_responder_latch_1_q1 ), .K2(K2_out),
    .Q2(\抢答判别模块_responder_latch_1_q2 ), .K3(K3_out), .Q3(\抢答判别模块_responder_latch_1_q3 ),
    .LOCK(\抢答判别模块_responder_latch_1_lock ), .ENABLE(\抢答判别模块_responder_latch_1_enable ));  // open: ALLOW
  \总记分模块___Score_Board  \u_总记分模块_score_board_1  (
    .ADD_SCORE(\加分按钮___ADD_SCORE_out ), .SUB_SCORE(\减分按钮___SUB_SCORE_out ),
    .RESET_SCORE(\总复位按钮___RESET_out ), .TEAM_SEL(\小组选择___TEAM_SEL_p3 ), ._1H(\总记分模块_score_board_1__1h ),
    ._2H(\总记分模块_score_board_1__2h ), ._3H(\总记分模块_score_board_1__3h ), ._4H(\总记分模块_score_board_1__4h ),
    ._1T(\总记分模块_score_board_1__1t ), ._2T(\总记分模块_score_board_1__2t ), ._3T(\总记分模块_score_board_1__3t ),
    ._4T(\总记分模块_score_board_1__4t ), ._1O(\总记分模块_score_board_1__1o ), ._2O(\总记分模块_score_board_1__2o ),
    ._3O(\总记分模块_score_board_1__3o ), ._4O(\总记分模块_score_board_1__4o ));
  Hex_Digit_Display hex_digit_display_13 (.value(\定时模块_p6 ));  // open: dp
  Hex_Digit_Display hex_digit_display_14 (.value(\定时模块_p7 ));  // open: dp
  LED \u_定时灯  (.in(\定时模块_p9 ));
  LED \u_时间到提示灯  (.in(\定时模块_p5 ));

  // Notes on the sheet:
  //   第 1 组
  //   第 3 组
  //   第 2 组
  //   第 4 组
  //   抢中指示灯
  //   抢答按钮
  //   正计时时间
endmodule

// 抢答判别模块
module \抢答判别模块___Responder_Latch  (
  input  START,
  input  RESET,
  input  K0,
  input  K1,
  input  K2,
  input  K3,
  output Q0,
  output Q1,
  output Q2,
  output Q3,
  output ALLOW,
  output LOCK,
  output ENABLE
);

  wire and_1_out, and_2_out, and_3_out, and_4_out, clock_1_out, not_1_out, not_2_out, not_3_out, or_2_out;

  Clock clock_1 (.out(clock_1_out));
  S_R_Flip_Flop s_r_ff_1 (.S(START), .clk(clock_1_out), .R(or_2_out), .Q(ALLOW));  // open: Qn, preset, reset
  not not_1 (not_1_out, K0);
  S_R_Flip_Flop u_Q0 (.S(and_1_out), .clk(clock_1_out), .R(RESET), .Q(Q0));  // open: Qn, preset, reset
  and and_1 (and_1_out, ENABLE, K0);
  S_R_Flip_Flop u_Q1 (.S(and_2_out), .clk(clock_1_out), .R(RESET), .Q(Q1));  // open: Qn, preset, reset
  and and_2 (and_2_out, ENABLE, K1, not_1_out);
  not not_2 (not_2_out, K1);
  and and_3 (and_3_out, ENABLE, K2, not_1_out, not_2_out);
  not not_3 (not_3_out, K2);
  S_R_Flip_Flop u_Q2 (.S(and_3_out), .clk(clock_1_out), .R(RESET), .Q(Q2));  // open: Qn, preset, reset
  S_R_Flip_Flop u_Q3 (.S(and_4_out), .clk(clock_1_out), .R(RESET), .Q(Q3));  // open: Qn, preset, reset
  and and_4 (and_4_out, ENABLE, K3, not_1_out, not_2_out, not_3_out);
  or or_1 (LOCK, Q0, Q1, Q2, Q3);
  or or_2 (or_2_out, RESET, LOCK);
  and and_5 (ENABLE, ALLOW, ~LOCK);  // AND_Gate

  // Notes on the sheet:
  //   K2: pull=down
  //   K1: pull=down
  //   RESET: pull=down
  //   K0: pull=down
  //   K3: pull=down
  //   START: pull=down
endmodule

module \抢答指示灯和声音模块___Responder_Indicator  (
  input  Q0,
  input  Q1,
  input  Q2,
  input  Q3,
  input  ENABLE,
  input  LOCK,
  input  FLASH_CLK,
  input  BEEP_CLK,
  output LED0,
  output LED1,
  output LED2,
  output LED3,
  output READY_LED,
  output BUZZER
);

  and and_1 (READY_LED, ENABLE, FLASH_CLK);
  and and_2 (BUZZER, BEEP_CLK, LOCK);

  assign LED0 = Q0;
  assign LED1 = Q1;
  assign LED2 = Q2;
  assign LED3 = Q3;
endmodule

module \定时模块___Timer  (
  input  BEEP_CLK,
  input  [1:0] TIME_SEL,
  input  SEC_CLK,
  input  TIMER_START,
  input  RESET,
  output TIME_UP,
  output TIME_ALARM,
  output [3:0] COUNT_ONES,
  output [3:0] COUNT_TENS,
  output RUN
);

  wire buzzer_1_p2, clock_1_out, comparator_1_eq, comparator_2_eq, COUNT_CLK_out, COUNT_ONES_tc, not_1_out,
       not_2_out, or_1_out, or_2_out;
  wire [3:0] multiplexer_1_out;

  Comparator #(.width(4), .mode("unsigned")) comparator_1 (
    .a(COUNT_TENS), .b(multiplexer_1_out), .eq(comparator_1_eq));  // open: gt, lt
  Multiplexer #(.select(2), .width(4), .enable("false")) multiplexer_1 (
    .in0(4'b0001), .in1(4'b0010), .in2(4'b0101), .in3(4'b0110), .out(multiplexer_1_out), .sel(TIME_SEL));
  Comparator #(.width(4), .mode("unsigned")) comparator_2 (
    .a(COUNT_ONES), .b(4'b0000), .eq(comparator_2_eq));  // open: gt, lt
  not not_1 (not_1_out, or_1_out);
  or or_1 (or_1_out, RESET, TIMER_START);
  Clock clock_1 (.out(clock_1_out));
  or or_2 (or_2_out, RESET, TIME_UP);
  and u_TIME_UP (TIME_UP, RUN, comparator_2_eq, comparator_1_eq);
  _74160 u_COUNT_ONES (
    .CLK(COUNT_CLK_out), .CLR(not_1_out), .LE(1'b1), .CEP(1'b1), .CET(1'b1), .Q1(COUNT_ONES[0]),
    .Q2(COUNT_ONES[1]), .Q3(COUNT_ONES[2]), .Q4(COUNT_ONES[3]), .TC(COUNT_ONES_tc));  // open: D1, D2, D3, D4
  and COUNT_CLK (COUNT_CLK_out, RUN, SEC_CLK);
  S_R_Flip_Flop s_r_ff_1 (.S(TIMER_START), .clk(clock_1_out), .R(or_2_out), .Q(RUN));  // open: Qn, preset, reset
  LED led_1 (.in(TIME_ALARM));
  S_R_Flip_Flop s_r_ff_2 (.S(TIME_UP), .clk(clock_1_out), .R(or_1_out), .Q(TIME_ALARM));  // open: Qn, preset, reset
  not not_2 (not_2_out, COUNT_ONES_tc);
  // Buzzer buzzer_1: pin names not known; wires that end beside it: 12'h999, buzzer_1_p2, {7{1'b1}}
  and and_1 (buzzer_1_p2, BEEP_CLK, TIME_ALARM);
  _74160 u_COUNT_TENS (
    .CLK(not_2_out), .CLR(not_1_out), .LE(1'b1), .CEP(1'b1), .CET(1'b1), .Q1(COUNT_TENS[0]),
    .Q2(COUNT_TENS[1]), .Q3(COUNT_TENS[2]), .Q4(COUNT_TENS[3]));  // open: D1, D2, D3, D4, TC

  // Notes on the sheet:
  //   TIMER_START: pull=down
  //   RESET: pull=down
endmodule

module \单组记分模块___Score_Counter  (
  input  ADD,
  input  SUB,
  input  RESET_SCORE,
  output [3:0] ONES,
  output [3:0] TENS,
  output [3:0] HUNDREDS
);

  wire and_1_out, and_2_out, and_3_out, and_4_out, and_5_out, and_6_out, buffer_1_out, buffer_2_out,
       comparator_1_eq, comparator_2_eq, comparator_3_eq, comparator_4_eq, comparator_5_eq, comparator_6_eq,
       HUNDREDS_STEP_out, IS_000_out, IS_999_out, not_1_out, not_2_out, or_1_out, TENS_STEP_out;

  and and_1 (and_1_out, ADD, not_1_out);
  and and_2 (and_2_out, SUB, not_2_out);
  or or_1 (or_1_out, and_1_out, and_2_out);
  Counter #(.width(4), .max('h9)) counter_1 (
    .load(1'b0), .D(4'b0000), .count(1'b1), .Q(ONES), .clk(or_1_out), .clr(RESET_SCORE), .down(and_2_out));  // open: carry, preset
  Comparator #(.width(4), .mode("unsigned")) comparator_1 (
    .a(ONES), .b(4'b1001), .eq(comparator_1_eq));  // open: gt, lt
  Comparator #(.width(4), .mode("unsigned")) comparator_2 (
    .a(ONES), .b(4'b0000), .eq(comparator_2_eq));  // open: gt, lt
  buf buffer_1 (buffer_1_out, or_1_out);
  or TENS_STEP (TENS_STEP_out, and_3_out, and_4_out);
  and and_3 (and_3_out, and_1_out, comparator_1_eq);
  and and_4 (and_4_out, and_2_out, comparator_2_eq);
  Counter #(.width(4), .max('h9)) counter_2 (
    .load(1'b0), .D(4'b0000), .count(TENS_STEP_out), .Q(TENS), .clk(buffer_1_out), .clr(RESET_SCORE),
    .down(and_2_out));  // open: carry, preset
  Comparator #(.width(4), .mode("unsigned")) comparator_3 (
    .a(TENS), .b(4'b1001), .eq(comparator_3_eq));  // open: gt, lt
  Comparator #(.width(4), .mode("unsigned")) comparator_4 (
    .a(TENS), .b(4'b0000), .eq(comparator_4_eq));  // open: gt, lt
  buf buffer_2 (buffer_2_out, buffer_1_out);
  or HUNDREDS_STEP (HUNDREDS_STEP_out, and_5_out, and_6_out);
  and and_5 (and_5_out, and_1_out, comparator_1_eq, comparator_3_eq);
  and and_6 (and_6_out, and_2_out, comparator_2_eq, comparator_4_eq);
  Counter #(.width(4), .max('h9)) counter_3 (
    .load(1'b0), .D(4'b0000), .count(HUNDREDS_STEP_out), .Q(HUNDREDS), .clk(buffer_2_out), .clr(RESET_SCORE),
    .down(and_2_out));  // open: carry, preset
  Comparator #(.width(4), .mode("unsigned")) comparator_5 (
    .a(HUNDREDS), .b(4'b1001), .eq(comparator_5_eq));  // open: gt, lt
  Comparator #(.width(4), .mode("unsigned")) comparator_6 (
    .a(HUNDREDS), .b(4'b0000), .eq(comparator_6_eq));  // open: gt, lt
  not not_1 (not_1_out, IS_999_out);
  and IS_999 (IS_999_out, comparator_5_eq, comparator_1_eq, comparator_3_eq);
  and IS_000 (IS_000_out, comparator_2_eq, comparator_4_eq, comparator_6_eq);
  not not_2 (not_2_out, IS_000_out);
endmodule

// 记分模块
module \总记分模块___Score_Board  (
  input  ADD_SCORE,
  input  SUB_SCORE,
  input  RESET_SCORE,
  input  [1:0] TEAM_SEL,
  output [3:0] _1H,
  output [3:0] _1T,
  output [3:0] _1O,
  output [3:0] _2H,
  output [3:0] _2T,
  output [3:0] _2O,
  output [3:0] _3H,
  output [3:0] _3T,
  output [3:0] _3O,
  output [3:0] _4H,
  output [3:0] _4T,
  output [3:0] _4O
);

  wire and_1_out, and_2_out, and_3_out, and_4_out, and_5_out, and_6_out, and_7_out, and_8_out,
       decoder_1_out0, decoder_1_out1, decoder_1_out2, decoder_1_out3;

  Decoder #(.select(2), .disabled(0)) decoder_1 (
    .out0(decoder_1_out0), .out1(decoder_1_out1), .out2(decoder_1_out2), .out3(decoder_1_out3),
    .sel(TEAM_SEL), .en(1'b1));
  and and_1 (and_1_out, ADD_SCORE, decoder_1_out0);
  and and_2 (and_2_out, SUB_SCORE, decoder_1_out0);
  and and_3 (and_3_out, ADD_SCORE, decoder_1_out1);
  and and_4 (and_4_out, SUB_SCORE, decoder_1_out1);
  and and_5 (and_5_out, ADD_SCORE, decoder_1_out2);
  and and_6 (and_6_out, SUB_SCORE, decoder_1_out2);
  and and_7 (and_7_out, ADD_SCORE, decoder_1_out3);
  and and_8 (and_8_out, SUB_SCORE, decoder_1_out3);
  \单组记分模块___Score_Counter  \u_单组记分模块_score_counter_1  (
    .ADD(and_1_out), .SUB(and_2_out), .RESET_SCORE(RESET_SCORE), .ONES(_1O), .TENS(_1T), .HUNDREDS(_1H));
  \单组记分模块___Score_Counter  \u_单组记分模块_score_counter_2  (
    .ADD(and_3_out), .SUB(and_4_out), .RESET_SCORE(RESET_SCORE), .ONES(_2O), .TENS(_2T), .HUNDREDS(_2H));
  \单组记分模块___Score_Counter  \u_单组记分模块_score_counter_3  (
    .ADD(and_5_out), .SUB(and_6_out), .RESET_SCORE(RESET_SCORE), .ONES(_3O), .TENS(_3T), .HUNDREDS(_3H));
  \单组记分模块___Score_Counter  \u_单组记分模块_score_counter_4  (
    .ADD(and_7_out), .SUB(and_8_out), .RESET_SCORE(RESET_SCORE), .ONES(_4O), .TENS(_4T), .HUNDREDS(_4H));
endmodule

module _74160 (
  input  CLK,
  input  CLR,
  input  LE,
  input  CEP,
  input  CET,
  input  D1,
  input  D2,
  input  D3,
  input  D4,
  output Q1,
  output Q2,
  output Q3,
  output Q4,
  output TC
);

  wire and_1_out, and_2_out, and_3_out, and_4_out, and_5_out, and_6_out, and_7_out, and_8_out, and_9_out,
       and_10_out, and_11_out, and_12_out, and_13_out, d_ff_4_qn, not_1_out, not_2_out, or_1_out, or_2_out,
       or_3_out, or_4_out, or_5_out, xor_1_out, xor_2_out, xor_3_out, xor_4_out;

  not not_1 (not_1_out, CLR);
  and and_1 (and_1_out, LE, CEP, CET);
  not not_2 (not_2_out, LE);
  and and_2 (and_2_out, D1, not_2_out);
  and and_3 (and_3_out, Q1, LE);
  and and_4 (and_4_out, D2, not_2_out);
  and and_5 (and_5_out, Q2, LE);
  and and_6 (and_6_out, Q1, and_1_out, d_ff_4_qn);
  and and_7 (and_7_out, D3, not_2_out);
  and and_8 (and_8_out, Q3, LE);
  and and_9 (and_9_out, Q2, Q1, and_1_out);
  and and_10 (and_10_out, D4, not_2_out);
  and and_11 (and_11_out, Q4, LE);
  and and_12 (and_12_out, Q3, Q2, Q1, and_1_out);
  and and_13 (and_13_out, Q4, Q1, and_1_out);
  xor xor_1 (xor_1_out, and_3_out, and_1_out);
  xor xor_2 (xor_2_out, and_5_out, and_6_out);
  xor xor_3 (xor_3_out, and_8_out, and_9_out);
  or or_1 (or_1_out, and_12_out, and_13_out);
  or or_2 (or_2_out, and_2_out, xor_1_out);
  or or_3 (or_3_out, and_4_out, xor_2_out);
  or or_4 (or_4_out, and_7_out, xor_3_out);
  or or_5 (or_5_out, and_10_out, xor_4_out);
  xor xor_4 (xor_4_out, and_11_out, or_1_out);
  D_Flip_Flop d_ff_1 (.clk(CLK), .D(or_2_out), .Q(Q1), .reset(not_1_out));  // open: Qn, preset
  D_Flip_Flop d_ff_2 (.clk(CLK), .D(or_3_out), .Q(Q2), .reset(not_1_out));  // open: Qn, preset
  D_Flip_Flop d_ff_3 (.clk(CLK), .D(or_4_out), .Q(Q3), .reset(not_1_out));  // open: Qn, preset
  D_Flip_Flop d_ff_4 (.clk(CLK), .D(or_5_out), .Q(Q4), .Qn(d_ff_4_qn), .reset(not_1_out));  // open: preset
  and and_14 (TC, Q4, Q1, CET);
endmodule

module _74161 (
  input  CLK,
  input  CLR,
  input  LE,
  input  CEP,
  input  CET,
  input  D1,
  input  D2,
  input  D3,
  input  D4,
  output Q1,
  output Q2,
  output Q3,
  output Q4,
  output TC
);

  wire and_1_out, and_2_out, and_3_out, and_4_out, and_5_out, and_6_out, and_7_out, and_8_out, and_9_out,
       and_10_out, and_11_out, and_12_out, not_1_out, not_2_out, or_1_out, or_2_out, or_3_out, or_4_out,
       xor_1_out, xor_2_out, xor_3_out, xor_4_out;

  not not_1 (not_1_out, CLR);
  and and_1 (and_1_out, LE, CEP, CET);
  not not_2 (not_2_out, LE);
  and and_2 (and_2_out, D1, not_2_out);
  and and_3 (and_3_out, Q1, LE);
  and and_4 (and_4_out, D2, not_2_out);
  and and_5 (and_5_out, Q2, LE);
  and and_6 (and_6_out, Q1, and_1_out);
  and and_7 (and_7_out, D3, not_2_out);
  and and_8 (and_8_out, Q3, LE);
  and and_9 (and_9_out, Q2, Q1, and_1_out);
  and and_10 (and_10_out, D4, not_2_out);
  and and_11 (and_11_out, Q4, LE);
  and and_12 (and_12_out, Q3, Q2, Q1, and_1_out);
  xor xor_1 (xor_1_out, and_3_out, and_1_out);
  xor xor_2 (xor_2_out, and_5_out, and_6_out);
  xor xor_3 (xor_3_out, and_8_out, and_9_out);
  xor xor_4 (xor_4_out, and_11_out, and_12_out);
  or or_1 (or_1_out, and_2_out, xor_1_out);
  or or_2 (or_2_out, and_4_out, xor_2_out);
  or or_3 (or_3_out, and_7_out, xor_3_out);
  or or_4 (or_4_out, and_10_out, xor_4_out);
  D_Flip_Flop d_ff_1 (.clk(CLK), .D(or_1_out), .Q(Q1), .reset(not_1_out));  // open: Qn, preset
  D_Flip_Flop d_ff_2 (.clk(CLK), .D(or_2_out), .Q(Q2), .reset(not_1_out));  // open: Qn, preset
  D_Flip_Flop d_ff_3 (.clk(CLK), .D(or_3_out), .Q(Q3), .reset(not_1_out));  // open: Qn, preset
  D_Flip_Flop d_ff_4 (.clk(CLK), .D(or_4_out), .Q(Q4), .reset(not_1_out));  // open: Qn, preset
  and and_13 (TC, Q4, Q3, Q2, Q1, CET);
endmodule

module \_7_段译码器  (
  input  A0,
  input  A1,
  input  A2,
  input  A3,
  output a,
  output b,
  output c,
  output d,
  output e,
  output f,
  output g
);

  // DisplayDecoder displaydecoder_1: pin names not known; wires that end beside it: {A3, A2, A1, A0}, a, b, c, d, e, f, g
endmodule

// HEX2BCD
module \HEX2BCD_60_以内  (
  input  D0,
  input  D1,
  input  D2,
  input  D3,
  input  D4,
  input  D5,
  input  D6,
  input  D7,
  output D0_2,
  output D1_2,
  output D2_2,
  output D3_2,
  output D4_2,
  output D5_2,
  output D6_2,
  output D7_2
);

  wire adder_1_cout, adder_2_cout, adder_3_cout, adder_4_cout, comparator_1_gt, comparator_2_gt,
       comparator_4_gt, comparator_5_gt, not_1_out, not_2_out;
  wire [2:0] and_2_out;
  wire [7:0] adder_1_out, adder_2_out, adder_3_out, adder_4_out, adder_5_out;

  Adder adder_1 (.a({D7, D6, D5, D4, D3, D2, D1, D0}), .b(8'h6), .out(adder_1_out), .cout(adder_1_cout));  // open: cin
  Adder adder_2 (
    .a({D7, D6, D5, D4, D3, D2, D1, D0}), .b(8'hc), .out(adder_2_out), .cin(adder_1_cout), .cout(adder_2_cout));
  Adder adder_3 (
    .a({D7, D6, D5, D4, D3, D2, D1, D0}), .b(8'h12), .out(adder_3_out), .cin(adder_2_cout),
    .cout(adder_3_cout));
  Adder adder_4 (
    .a({D7, D6, D5, D4, D3, D2, D1, D0}), .b(8'h18), .out(adder_4_out), .cin(adder_3_cout),
    .cout(adder_4_cout));
  Adder adder_5 (.a({D7, D6, D5, D4, D3, D2, D1, D0}), .b(8'h1e), .out(adder_5_out), .cin(adder_4_cout));  // open: cout
  Comparator comparator_1 (.a({D7, D6, D5, D4, D3, D2, D1, D0}), .b(8'h9), .gt(comparator_1_gt));  // open: eq, lt
  Comparator comparator_2 (.a({D7, D6, D5, D4, D3, D2, D1, D0}), .b(8'h13), .gt(comparator_2_gt));  // open: eq, lt
  Comparator comparator_3 (.a({D7, D6, D5, D4, D3, D2, D1, D0}), .b(8'h1d), .gt(and_2_out[2]));  // open: eq, lt
  not not_1 (not_1_out, comparator_4_gt);
  Comparator comparator_4 (.a({D7, D6, D5, D4, D3, D2, D1, D0}), .b(8'h27), .gt(comparator_4_gt));  // open: eq, lt
  not not_2 (not_2_out, comparator_5_gt);
  Comparator comparator_5 (.a({D7, D6, D5, D4, D3, D2, D1, D0}), .b(8'h31), .gt(comparator_5_gt));  // open: eq, lt
  Multiplexer #(.select(3), .width(8), .disabled(0), .enable("false")) multiplexer_1 (
    .in0({D7, D6, D5, D4, D3, D2, D1, D0}), .in1(adder_1_out), .in3(adder_2_out), .in4(adder_5_out),
    .in6(adder_4_out), .in7(adder_3_out), .out({D7_2, D6_2, D5_2, D4_2, D3_2, D2_2, D1_2, D0_2}),
    .sel(and_2_out));  // open: in2, in5
  and and_1 (and_2_out[1], comparator_2_gt, not_2_out);
  and and_2 (and_2_out[0], comparator_1_gt, not_1_out);
endmodule
